// Logisim project CPU.circ as structural Verilog: 11 circuits, main circuit GRF
module GRF (
  input  clk,
  input  we,
  input  reset,
  input  [4:0] a1,
  input  [4:0] a2,
  input  [4:0] a3,
  input  [31:0] wd,
  input  [31:0] in_8,
  output [31:0] rd1,
  output [31:0] rd2
);

  wire [4:0] multiplexer_1_out;
  wire [31:0] _0, _1, _2, _3, _4, _5, _6, _7, _8, _9, _10, _11, _12, _13, _14, _15, _16, _17, _18, _19, _20,
       _21, _22, _23, _24, _25, _26, _27, _28, _29, _30, _31, demultiplexer_1_out1, demultiplexer_1_out2,
       demultiplexer_1_out3, demultiplexer_1_out4, demultiplexer_1_out5, demultiplexer_1_out6,
       demultiplexer_1_out7, demultiplexer_1_out8, demultiplexer_1_out9, demultiplexer_1_out10,
       demultiplexer_1_out11, demultiplexer_1_out12, demultiplexer_1_out13, demultiplexer_1_out14,
       demultiplexer_1_out15, demultiplexer_1_out16, demultiplexer_1_out17, demultiplexer_1_out18,
       demultiplexer_1_out19, demultiplexer_1_out20, demultiplexer_1_out21, demultiplexer_1_out22,
       demultiplexer_1_out23, demultiplexer_1_out24, demultiplexer_1_out25, demultiplexer_1_out26,
       demultiplexer_1_out27, demultiplexer_1_out28, demultiplexer_1_out29, demultiplexer_1_out30,
       demultiplexer_1_out31;

  Demultiplexer #(.select(5), .width(32), .tristate("true")) demultiplexer_1 (
    .out1(demultiplexer_1_out1), .out2(demultiplexer_1_out2), .out3(demultiplexer_1_out3),
    .out4(demultiplexer_1_out4), .out5(demultiplexer_1_out5), .out6(demultiplexer_1_out6),
    .out7(demultiplexer_1_out7), .out8(demultiplexer_1_out8), .out9(demultiplexer_1_out9),
    .out10(demultiplexer_1_out10), .out11(demultiplexer_1_out11), .out12(demultiplexer_1_out12),
    .out13(demultiplexer_1_out13), .out14(demultiplexer_1_out14), .out15(demultiplexer_1_out15),
    .out16(demultiplexer_1_out16), .out17(demultiplexer_1_out17), .out18(demultiplexer_1_out18),
    .out19(demultiplexer_1_out19), .out20(demultiplexer_1_out20), .out21(demultiplexer_1_out21),
    .out22(demultiplexer_1_out22), .out23(demultiplexer_1_out23), .out24(demultiplexer_1_out24),
    .out25(demultiplexer_1_out25), .out26(demultiplexer_1_out26), .out27(demultiplexer_1_out27),
    .out28(demultiplexer_1_out28), .out29(demultiplexer_1_out29), .out30(demultiplexer_1_out30),
    .out31(demultiplexer_1_out31), .in(wd), .sel(multiplexer_1_out));  // open: out0, en
  Multiplexer #(.width(5), .disabled(0)) multiplexer_1 (
    .in0({5{1'b0}}), .in1(a3), .out(multiplexer_1_out), .sel(we));  // open: en
  // Probe on demultiplexer_1_out1
  // Probe on _1
  Reg reg_1 (
    .in_1(demultiplexer_1_out1), .in_2(demultiplexer_1_out2), .in_3(demultiplexer_1_out3),
    .in_4(demultiplexer_1_out4), .in_5(demultiplexer_1_out5), .in_6(demultiplexer_1_out6),
    .in_7(demultiplexer_1_out7), .in_8(demultiplexer_1_out8), .in_9(demultiplexer_1_out9),
    .in_10(demultiplexer_1_out10), .in_11(demultiplexer_1_out11), .in_12(demultiplexer_1_out12),
    .in_13(demultiplexer_1_out13), .in_14(demultiplexer_1_out14), .in_15(demultiplexer_1_out15),
    .in_18(demultiplexer_1_out16), .in_19(demultiplexer_1_out17), .in_20(demultiplexer_1_out18),
    .in_21(demultiplexer_1_out19), .in_22(demultiplexer_1_out20), .in_23(demultiplexer_1_out21),
    .in_24(demultiplexer_1_out22), .in_25(demultiplexer_1_out23), .in_26(demultiplexer_1_out24),
    .in_27(demultiplexer_1_out25), .in_28(demultiplexer_1_out26), .in_29(demultiplexer_1_out27),
    .in_30(demultiplexer_1_out28), .in_31(demultiplexer_1_out29), .in_32(demultiplexer_1_out30),
    .in_33(demultiplexer_1_out31), .in_16(clk), .in_17(reset), .out_34(_0), .out_35(_1), .out_36(_2),
    .out_37(_3), .out_38(_4), .out_39(_5), .out_40(_6), .out_41(_7), .out_42(_8), .out_43(_9), .out_44(_10),
    .out_45(_11), .out_46(_12), .out_47(_13), .out_48(_14), .out_49(_15), .out_50(_16), .out_51(_17),
    .out_52(_18), .out_53(_19), .out_54(_20), .out_55(_21), .out_56(_22), .out_57(_23), .out_58(_24),
    .out_59(_25), .out_60(_26), .out_61(_27), .out_62(_28), .out_63(_29), .out_64(_30), .out_65(_31));
  Multiplexer #(.select(5), .width(32), .disabled(0)) multiplexer_2 (
    .in0(_0), .in1(_1), .in2(_2), .in3(_3), .in4(_4), .in5(_5), .in6(_6), .in7(_7), .in8(_8), .in9(_9),
    .in10(_10), .in11(_11), .in12(_12), .in13(_13), .in14(_14), .in15(_15), .in16(_16), .in17(_17),
    .in18(_18), .in19(_19), .in20(_20), .in21(_21), .in22(_22), .in23(_23), .in24(_24), .in25(_25),
    .in26(_26), .in27(_27), .in28(_28), .in29(_29), .in30(_30), .in31(_31), .out(rd1), .sel(a1));  // open: en
  Multiplexer #(.select(5), .width(32), .disabled(0)) multiplexer_3 (
    .in0(_0), .in1(_1), .in2(_2), .in3(_3), .in4(_4), .in5(_5), .in6(_6), .in7(_7), .in8(_8), .in9(_9),
    .in10(_10), .in11(_11), .in12(_12), .in13(_13), .in14(_14), .in15(_15), .in16(_16), .in17(_17),
    .in18(_18), .in19(_19), .in20(_20), .in21(_21), .in22(_22), .in23(_23), .in24(_24), .in25(_25),
    .in26(_26), .in27(_27), .in28(_28), .in29(_29), .in30(_30), .in31(_31), .out(rd2), .sel(a2));  // open: en
endmodule

module Reg (
  input  [31:0] in_1,
  input  [31:0] in_2,
  input  [31:0] in_3,
  input  [31:0] in_4,
  input  [31:0] in_5,
  input  [31:0] in_6,
  input  [31:0] in_7,
  input  [31:0] in_8,
  input  [31:0] in_9,
  input  [31:0] in_10,
  input  [31:0] in_11,
  input  [31:0] in_12,
  input  [31:0] in_13,
  input  [31:0] in_14,
  input  [31:0] in_15,
  input  in_16,
  input  in_17,
  input  [31:0] in_18,
  input  [31:0] in_19,
  input  [31:0] in_20,
  input  [31:0] in_21,
  input  [31:0] in_22,
  input  [31:0] in_23,
  input  [31:0] in_24,
  input  [31:0] in_25,
  input  [31:0] in_26,
  input  [31:0] in_27,
  input  [31:0] in_28,
  input  [31:0] in_29,
  input  [31:0] in_30,
  input  [31:0] in_31,
  input  [31:0] in_32,
  input  [31:0] in_33,
  output [31:0] out_34,
  output [31:0] out_35,
  output [31:0] out_36,
  output [31:0] out_37,
  output [31:0] out_38,
  output [31:0] out_39,
  output [31:0] out_40,
  output [31:0] out_41,
  output [31:0] out_42,
  output [31:0] out_43,
  output [31:0] out_44,
  output [31:0] out_45,
  output [31:0] out_46,
  output [31:0] out_47,
  output [31:0] out_48,
  output [31:0] out_49,
  output [31:0] out_50,
  output [31:0] out_51,
  output [31:0] out_52,
  output [31:0] out_53,
  output [31:0] out_54,
  output [31:0] out_55,
  output [31:0] out_56,
  output [31:0] out_57,
  output [31:0] out_58,
  output [31:0] out_59,
  output [31:0] out_60,
  output [31:0] out_61,
  output [31:0] out_62,
  output [31:0] out_63,
  output [31:0] out_64,
  output [31:0] out_65
);

  Register #(.width(32)) register_1 (.D({32{1'b0}}), .Q(out_34), .clk(in_16), .clr(in_17));  // open: en
  Register #(.width(32)) register_2 (.D(in_3), .Q(out_37), .clk(in_16), .clr(in_17));  // open: en
  Register #(.width(32)) register_3 (.D(in_6), .Q(out_40), .clk(in_16), .clr(in_17));  // open: en
  Register #(.width(32)) register_4 (.D(in_9), .Q(out_43), .clk(in_16), .clr(in_17));  // open: en
  Register #(.width(32)) register_5 (.D(in_12), .Q(out_46), .clk(in_16), .clr(in_17));  // open: en
  Register #(.width(32)) register_6 (.D(in_15), .Q(out_49), .clk(in_16), .clr(in_17));  // open: en
  Register #(.width(32)) register_7 (.D(in_18), .Q(out_50), .clk(in_16), .clr(in_17));  // open: en
  Register #(.width(32)) register_8 (.D(in_21), .Q(out_53), .clk(in_16), .clr(in_17));  // open: en
  Register #(.width(32)) register_9 (.D(in_24), .Q(out_56), .clk(in_16), .clr(in_17));  // open: en
  Register #(.width(32)) register_10 (.D(in_27), .Q(out_59), .clk(in_16), .clr(in_17));  // open: en
  Register #(.width(32)) register_11 (.D(in_30), .Q(out_62), .clk(in_16), .clr(in_17));  // open: en
  Register #(.width(32)) register_12 (.D(in_19), .Q(out_51), .clk(in_16), .clr(in_17));  // open: en
  Register #(.width(32)) register_13 (.D(in_22), .Q(out_54), .clk(in_16), .clr(in_17));  // open: en
  Register #(.width(32)) register_14 (.D(in_25), .Q(out_57), .clk(in_16), .clr(in_17));  // open: en
  Register #(.width(32)) register_15 (.D(in_28), .Q(out_60), .clk(in_16), .clr(in_17));  // open: en
  Register #(.width(32)) register_16 (.D(in_31), .Q(out_63), .clk(in_16), .clr(in_17));  // open: en
  Register #(.width(32)) register_17 (.D(in_1), .Q(out_35), .clk(in_16), .clr(in_17));  // open: en
  Register #(.width(32)) register_18 (.D(in_4), .Q(out_38), .clk(in_16), .clr(in_17));  // open: en
  Register #(.width(32)) register_19 (.D(in_7), .Q(out_41), .clk(in_16), .clr(in_17));  // open: en
  Register #(.width(32)) register_20 (.D(in_10), .Q(out_44), .clk(in_16), .clr(in_17));  // open: en
  Register #(.width(32)) register_21 (.D(in_13), .Q(out_47), .clk(in_16), .clr(in_17));  // open: en
  Register #(.width(32)) register_22 (.D(in_14), .Q(out_48), .clk(in_16), .clr(in_17));  // open: en
  Register #(.width(32)) register_23 (.D(in_20), .Q(out_52), .clk(in_16), .clr(in_17));  // open: en
  Register #(.width(32)) register_24 (.D(in_23), .Q(out_55), .clk(in_16), .clr(in_17));  // open: en
  Register #(.width(32)) register_25 (.D(in_26), .Q(out_58), .clk(in_16), .clr(in_17));  // open: en
  Register #(.width(32)) register_26 (.D(in_29), .Q(out_61), .clk(in_16), .clr(in_17));  // open: en
  Register #(.width(32)) register_27 (.D(in_32), .Q(out_64), .clk(in_16), .clr(in_17));  // open: en
  Register #(.width(32)) register_28 (.D(in_2), .Q(out_36), .clk(in_16), .clr(in_17));  // open: en
  Register #(.width(32)) register_29 (.D(in_5), .Q(out_39), .clk(in_16), .clr(in_17));  // open: en
  Register #(.width(32)) register_30 (.D(in_8), .Q(out_42), .clk(in_16), .clr(in_17));  // open: en
  Register #(.width(32)) register_31 (.D(in_11), .Q(out_45), .clk(in_16), .clr(in_17));  // open: en
  Register #(.width(32)) register_32 (.D(in_33), .Q(out_65), .clk(in_16), .clr(in_17));  // open: en

  // Other names for the same wires on the sheet: clk = in_16; reset = in_17
endmodule

module IFU (
  input  jal,
  input  clk,
  input  reset,
  input  [25:0] in_4,
  input  in_5,
  input  in_6,
  input  jr,
  input  [31:0] in_8,
  output [31:0] Instr,
  output [31:0] pc
);

  wire comparator_1_gt;
  wire [11:0] subtractor_1_out_2;
  wire [31:0] npc_1_npc, PC_q, subtractor_1_out;

  Register #(.width(32)) u_PC (.D(npc_1_npc), .Q(PC_q), .clk(clk), .clr(reset));  // open: en
  Comparator #(.width(32), .mode("unsigned")) comparator_1 (
    .a(PC_q), .b({32{1'b0}}), .gt(comparator_1_gt));  // open: eq, lt
  Multiplexer #(.width(32), .disabled(0)) multiplexer_1 (
    .in0(32'h3000), .in1(PC_q), .out(pc), .sel(comparator_1_gt));  // open: en
  NPC npc_1 (.pc(pc), .offest(in_4), .result(in_5), .beq(in_6), .in_1(jr), .in_2(in_8), .in_7(jal), .NPC(npc_1_npc));
  Subtractor #(.width(32)) subtractor_1 (
    .a(pc), .b(32'h3000), .out({subtractor_1_out[31:14], subtractor_1_out_2, subtractor_1_out[1:0]}));  // open: bin, bout
  ROM #(.addrWidth(12), .dataWidth(32)) rom_1 (.addr(subtractor_1_out_2), .data(Instr));  // open: sel

  // Other names for the same wires on the sheet: beq = in_6; offest[25:0] = in_4; RegRs[31:0] = in_8; result = in_5

  // Notes on the sheet:
  //   contents of rom_1 (hex, n*v repeats v):
  //   12a4020 1484822 3c090001 10090003 8d280000 ad490000 0 350b0001
endmodule

module NPC (
  input  in_1,
  input  [31:0] in_2,
  input  [31:0] pc,
  input  [25:0] offest,
  input  result,
  input  beq,
  input  in_7,
  output [31:0] NPC
);

  wire and_1_out;
  wire [31:0] adder_1_out, adder_3_out, bit_extender_1_out, bit_extender_2_out, jalpc, multiplexer_1_out,
       multiplexer_2_out, shifter_1_out, shifter_2_out, shifter_3_out, shifter_4_out;

  // Probe on bit_extender_1_out
  assign bit_extender_1_out = {{16{offest[15]}}, offest[15:0]};  // Bit_Extender bit_extender_1
  Shifter #(.width(32)) shifter_1 (.in(bit_extender_1_out), .\dist (5'b00010), .out(shifter_1_out));
  Shifter #(.width(32), .shift("lr")) shifter_2 (.in(pc), .\dist (5'b11100), .out(shifter_2_out));
  assign bit_extender_2_out = {{6{1'b0}}, offest};  // Bit_Extender bit_extender_2
  Shifter #(.width(32)) shifter_3 (.in(shifter_2_out), .\dist (5'b11100), .out(shifter_3_out));
  Shifter #(.width(32)) shifter_4 (.in(bit_extender_2_out), .\dist (5'b00010), .out(shifter_4_out));
  Adder #(.width(32)) adder_1 (.a(pc), .b(32'h4), .out(adder_1_out));  // open: cin, cout
  and and_1 (and_1_out, result, beq);
  Adder #(.width(32)) adder_2 (.a(shifter_3_out), .b(shifter_4_out), .out(jalpc));  // open: cin, cout
  Multiplexer #(.width(32), .disabled(0)) multiplexer_1 (
    .in0({32{1'b0}}), .in1(shifter_1_out), .out(multiplexer_1_out), .sel(and_1_out));  // open: en
  Adder #(.width(32)) adder_3 (.a(adder_1_out), .b(multiplexer_1_out), .out(adder_3_out));  // open: cin, cout
  Multiplexer #(.width(32)) multiplexer_2 (
    .in0(adder_3_out), .in1(in_2), .out(multiplexer_2_out), .sel(in_1));  // open: en
  Multiplexer #(.width(32)) multiplexer_3 (.in0(multiplexer_2_out), .in1(jalpc), .out(NPC), .sel(in_7));  // open: en

  // Other names for the same wires on the sheet: imm16[15:0] = offest[15:0]; imm26[25:0] = offest; jal = in_7;
  //   jr = in_1; RegRs[31:0] = in_2
endmodule

module ALU (
  input  cin,
  input  aluop,
  input  lui,
  input  [31:0] w1,
  input  [31:0] w2,
  output result,
  output [31:0] aluout
);

  wire [31:0] adder_1_out, adder_2_out, bit_extender_1_out, multiplexer_1_out, multiplexer_2_out, not_1_out,
       or_1_out, shifter_1_out;

  assign bit_extender_1_out = {{31{1'b0}}, cin};  // Bit_Extender bit_extender_1
  assign not_1_out = ~w2;  // NOT_Gate not_1, 32 bits wide
  Adder #(.width(32)) adder_1 (.a(bit_extender_1_out), .b(w1), .out(adder_1_out));  // open: cin, cout
  Multiplexer #(.width(32), .disabled(0)) multiplexer_1 (
    .in0(w2), .in1(not_1_out), .out(multiplexer_1_out), .sel(cin));  // open: en
  Adder #(.width(32)) adder_2 (.a(adder_1_out), .b(multiplexer_1_out), .out(adder_2_out));  // open: cin, cout
  assign or_1_out = w1 | w2;  // OR_Gate or_1, 32 bits wide
  Comparator #(.width(32)) comparator_1 (.a({32{1'b0}}), .b(adder_2_out), .eq(result));  // open: gt, lt
  Multiplexer #(.width(32), .disabled(0)) multiplexer_2 (
    .in0(adder_2_out), .in1(or_1_out), .out(multiplexer_2_out), .sel(aluop));  // open: en
  Shifter #(.width(32)) shifter_1 (.in(w2), .\dist (5'b10000), .out(shifter_1_out));
  Multiplexer #(.width(32), .disabled(0)) multiplexer_3 (
    .in0(multiplexer_2_out), .in1(shifter_1_out), .out(aluout), .sel(lui));  // open: en
endmodule

module Controller (
  input  [5:0] in_1,
  input  [5:0] in_2,
  output sw,
  output beq,
  output WD,
  output lui,
  output jr,
  output jal,
  output aluop,
  output EXTop,
  output Bsel,
  output we,
  output RegC,
  output cin
);

  wire and_1_add, and_1_beq, and_1_jal, and_1_jr, and_1_lui, and_1_lw, and_1_ori, and_1_sub, and_1_sw;

  AND and_1 (
    .opcode(in_1), .funct(in_2), .add(and_1_add), .sub(and_1_sub), .beq(and_1_beq), .lw(and_1_lw),
    .sw(and_1_sw), .lui(and_1_lui), .ori(and_1_ori), .jr(and_1_jr), .jal(and_1_jal));  // open: nop
  OR or_1 (
    .add(and_1_add), .sub(and_1_sub), .beq(and_1_beq), .lw(and_1_lw), .sw(and_1_sw), .lui(and_1_lui),
    .ori(and_1_ori), .jr(and_1_jr), .jal(and_1_jal), .sw_2(sw), .aluop(aluop), .EXTop(EXTop), .cin(cin),
    .Bsel(Bsel), .we(we), .RegC(RegC), .beq_2(beq), .WD(WD), .lui_2(lui), .jr_2(jr), .jal_2(jal));
endmodule

module main (
  input  in_1,
  output [31:0] out_2,
  output [31:0] out_3,
  output RegWrite,
  output [4:0] out_5,
  output [31:0] out_6,
  output MemWrite,
  output [31:0] MemAddr,
  output [31:0] MemData
);

  wire aluop, beq, Bsel, cin, clk, EXTop, jal, jr, lui, RegC, result, WD;
  wire [4:0] multiplexer_1_out, rd, rs, rt, shamt;
  wire [5:0] funct, opcode;
  wire [15:0] imm16;
  wire [25:0] imm26;
  wire [31:0] DMout, ext_1_out_3, multiplexer_3_out, multiplexer_5_out, pc31, RegRs;

  Clock clock_1 (.out(clk));
  Multiplexer #(.width(5), .disabled(0)) multiplexer_1 (
    .in0(rt), .in1(rd), .out(multiplexer_1_out), .sel(RegC));  // open: en
  Multiplexer #(.width(5), .disabled(0)) multiplexer_2 (
    .in0(multiplexer_1_out), .in1({5{1'b1}}), .out(out_5), .sel(jal));  // open: en
  IFU ifu_1 (
    .clk(clk), .reset(in_1), .in_4(imm26), .in_5(result), .in_6(beq), .jal(jal), .jr(jr), .in_8(RegRs),
    .Instr(out_2), .pc(out_3));
  // Probe on out_2
  Adder #(.width(32)) adder_1 (.a(out_3), .b(32'h4), .out(pc31));  // open: cin, cout
  Multiplexer #(.width(32), .disabled(0)) multiplexer_3 (
    .in0(MemAddr), .in1(DMout), .out(multiplexer_3_out), .sel(WD));  // open: en
  Multiplexer #(.width(32)) multiplexer_4 (.in0(multiplexer_3_out), .in1(pc31), .out(out_6), .sel(jal));  // open: en
  // Probe on imm16
  // Probe on imm16
  Splitter splitter_1 (
    .in_1(out_2), .out_9(imm26), .imm16(imm16), .funct(funct), .shamt(shamt), .rd(rd), .rt(rt), .rs(rs),
    .opcode(opcode));
  GRF grf_1 (
    .a1(rs), .a2(rt), .a3(out_5), .wd(out_6), .in_8(out_3), .clk(clk), .reset(in_1), .we(RegWrite),
    .rd1(RegRs), .rd2(MemData));
  EXT ext_1 (.in_1(imm16), .in_2(EXTop), .out_3(ext_1_out_3));
  Multiplexer #(.width(32), .disabled(0)) multiplexer_5 (
    .in0(MemData), .in1(ext_1_out_3), .out(multiplexer_5_out), .sel(Bsel));  // open: en
  // Probe on ext_1_out_3
  ALU alu_1 (
    .w1(RegRs), .w2(multiplexer_5_out), .cin(cin), .aluop(aluop), .lui(lui), .result(result), .aluout(MemAddr));
  Controller controller_1 (
    .in_1(opcode), .in_2(funct), .sw(MemWrite), .aluop(aluop), .EXTop(EXTop), .cin(cin), .Bsel(Bsel),
    .we(RegWrite), .RegC(RegC), .beq(beq), .WD(WD), .lui(lui), .jr(jr), .jal(jal));
  RAM #(.addrWidth(14), .dataWidth(32), .bus("separate")) ram_1 (
    .addr(MemAddr[15:2]), .din(MemData), .data(DMout), .str(MemWrite), .clk(clk), .ld(WD), .clr(in_1));  // open: sel

  // Other names for the same wires on the sheet: ALUout[31:0] = MemAddr; DMinput[31:0] = MemData; Instr[31:0] = out_2;
  //   pc[31:0] = out_3; RegAddr[4:0] = out_5; RegData[31:0] = out_6; reset = in_1; sw = MemWrite; we = RegWrite
endmodule

module Splitter (
  input  [31:0] in_1,
  output [15:0] imm16,
  output [5:0] funct,
  output [4:0] shamt,
  output [4:0] rd,
  output [4:0] rt,
  output [4:0] rs,
  output [5:0] opcode,
  output [25:0] out_9
);


  assign funct = in_1[5:0];
  assign imm16 = in_1[15:0];
  assign opcode = in_1[31:26];
  assign out_9 = in_1[25:0];
  assign rd = in_1[15:11];
  assign rs = in_1[25:21];
  assign rt = in_1[20:16];
  assign shamt = in_1[10:6];

  // Other names for the same wires on the sheet: imm26[25:0] = in_1[25:0]; imm32[31:0] = in_1
endmodule

module AND (
  input  [5:0] opcode,
  input  [5:0] funct,
  output nop,
  output add,
  output sub,
  output beq,
  output lw,
  output sw,
  output lui,
  output ori,
  output jr,
  output jal
);

  wire comparator_1_eq, comparator_2_eq, comparator_3_eq, comparator_4_eq, comparator_5_eq, comparator_6_eq,
       comparator_12_eq, comparator_13_eq;

  Comparator #(.width(6)) comparator_1 (.a(opcode), .b({6{1'b0}}), .eq(comparator_1_eq));  // open: gt, lt
  Comparator #(.width(6)) comparator_2 (.a(funct), .b({6{1'b0}}), .eq(comparator_2_eq));  // open: gt, lt
  Comparator #(.width(6)) comparator_3 (.a(opcode), .b({6{1'b0}}), .eq(comparator_3_eq));  // open: gt, lt
  Comparator #(.width(6)) comparator_4 (.a(funct), .b(6'b100000), .eq(comparator_4_eq));  // open: gt, lt
  Comparator #(.width(6)) comparator_5 (.a(opcode), .b({6{1'b0}}), .eq(comparator_5_eq));  // open: gt, lt
  Comparator #(.width(6), .mode("unsigned")) comparator_6 (
    .a(funct), .b(6'b100010), .eq(comparator_6_eq));  // open: gt, lt
  Comparator #(.width(6)) comparator_7 (.a(opcode), .b(6'b000100), .eq(beq));  // open: gt, lt
  Comparator #(.width(6)) comparator_8 (.a(opcode), .b(6'b100011), .eq(lw));  // open: gt, lt
  Comparator #(.width(6)) comparator_9 (.a(opcode), .b(6'b101011), .eq(sw));  // open: gt, lt
  Comparator #(.width(6)) comparator_10 (.a(opcode), .b(6'b001111), .eq(lui));  // open: gt, lt
  Comparator #(.width(6)) comparator_11 (.a(opcode), .b(6'b001101), .eq(ori));  // open: gt, lt
  Comparator #(.width(6)) comparator_12 (.a(opcode), .b({6{1'b0}}), .eq(comparator_12_eq));  // open: gt, lt
  Comparator #(.width(6), .mode("unsigned")) comparator_13 (
    .a(funct), .b(6'b001000), .eq(comparator_13_eq));  // open: gt, lt
  Comparator #(.width(6)) comparator_14 (.a(opcode), .b(6'b000011), .eq(jal));  // open: gt, lt
  and and_1 (nop, comparator_1_eq, comparator_2_eq);
  and and_2 (add, comparator_3_eq, comparator_4_eq);
  and and_3 (sub, comparator_5_eq, comparator_6_eq);
  and and_4 (jr, comparator_12_eq, comparator_13_eq);
endmodule

module OR (
  input  add,
  input  sub,
  input  beq,
  input  lw,
  input  sw,
  input  lui,
  input  ori,
  input  jr,
  input  jal,
  output sw_2,
  output beq_2,
  output WD,
  output lui_2,
  output jr_2,
  output jal_2,
  output aluop,
  output EXTop,
  output cin,
  output Bsel,
  output we,
  output RegC
);

  or or_1 (EXTop, sw, lw);
  or or_2 (cin, beq, sub);
  or or_3 (Bsel, ori, sw, lw, lui);
  or or_4 (we, jal, add, sub, lw, lui, ori);
  or or_5 (RegC, add, sub);

  assign aluop = ori;
  assign beq_2 = beq;
  assign jal_2 = jal;
  assign jr_2 = jr;
  assign lui_2 = lui;
  assign sw_2 = sw;
  assign WD = lw;
endmodule

module EXT (
  input  [15:0] in_1,
  input  in_2,
  output [31:0] out_3
);

  wire [31:0] bit_extender_1_out, bit_extender_2_out;

  assign bit_extender_1_out = {{16{1'b0}}, in_1};  // Bit_Extender bit_extender_1
  assign bit_extender_2_out = {{16{in_1[15]}}, in_1};  // Bit_Extender bit_extender_2
  Multiplexer #(.width(32), .disabled(0)) multiplexer_1 (
    .in0(bit_extender_1_out), .in1(bit_extender_2_out), .out(out_3), .sel(in_2));  // open: en
endmodule
